# Fritzing sketch InlineFan (saved by Fritzing 1.0.2b)
breadboards: 1

parts:
  WeMos_D1_Mini1 = WeMos D1 Mini
  Q1 = NPN-Transistor [part_number=BC337 package="SOT-23 [SMD]"]
  R1 = Resistor [tolerance=±5% power=0.25W resistance=100 package=THT]
  J2 = female pin header, 2 pins [form="♀ (female)"]
  J3 = female pin header, 2 pins [form="♀ (female)"]
  U1 = LM2596 step down module

nets:
  N1: WeMos_D1_Mini1.5V, U1.OUT+
  N2: WeMos_D1_Mini1.D0, Q1.0
  N3: WeMos_D1_Mini1.G, J3.pin1, U1.IN-, U1.OUT-
  N4: Q1.2, R1.Pin_1
  N5: Q1.1, J2.pin1
  N6: R1.Pin_0, J2.pin2
  N7: J3.pin2, U1.IN+

notes:
  GND, VCC 24v
  R+, R-

custom parts:
  LM2596 step down module: LM2596 DC-DC step down power supply module 3 A.
